# Fritzing sketch schematics (saved by Fritzing 0.9.5d)
breadboards: 1

parts:
  Part1 = Thumb Joystick
  LED1 = smd LED [color="Red (633nm)" package="0805 [SMD]"]
  LED2 = smd LED [color="Green (555nm)" package="0805 [SMD]"]
  Part2 = Arduino Nano (Rev3.0)
  R1 = Resistor [tolerance=±5% resistance=220 package="0402 [SMD]"]
  R2 = Resistor [tolerance=±5% resistance=220 package="0402 [SMD]"]

nets:
  GND: Part1.GND, Part2.GND
  N1: Part1.SEL, Part2.D9
  N2: Part1.HORZ, Part2.A7
  N3: Part1.VERT, Part2.A6
  VCC: Part1.VCC, LED1.cathode, LED2.cathode, Part2.5V
  N4: LED1.anode, R2.Pin_1
  N5: LED2.anode, R1.Pin_1
  N6: Part2.D5, R2.Pin_0
  N7: Part2.D6, R1.Pin_0
